// Logisim project 1)all gates2.circ as structural Verilog: 1 circuit, main circuit main
module main (
  input  x,
  input  x_2,
  input  y,
  input  x_3,
  input  x_4,
  input  y_2,
  input  y_3,
  input  x_5,
  input  y_4,
  output y_5,
  output \nand ,
  output z,
  output \or ,
  output \and 
);

  not not_1 (y_5, x);
  or or_1 (\or , x_4, y_3);
  and and_1 (\and , x_5, y_4);
  nand nand_1 (\nand , x_2, y);
  nor nor_1 (z, x_3, y_2);
endmodule
