// Logisim project 13)Two bit half subtractor.circ as structural Verilog: 1 circuit, main circuit main
module main (
  input  x,
  input  y,
  output d,
  output b
);

  wire not_1_out;

  not not_1 (not_1_out, x);
  xor xor_1 (d, x, y);
  and and_1 (b, not_1_out, y);
endmodule
