// Logisim project 14)Full adder.circ as structural Verilog: 1 circuit, main circuit main
module main (
  input  a,
  input  b,
  input  c,
  output s,
  output ca
);

  wire and_1_out, and_2_out, xor_1_out;

  and and_1 (and_1_out, a, b);
  xor xor_1 (xor_1_out, a, b);
  xor xor_2 (s, xor_1_out, c);
  and and_2 (and_2_out, xor_1_out, c);
  or or_1 (ca, and_2_out, and_1_out);
endmodule
