// Logisim project 15)Full subtractor.circ as structural Verilog: 1 circuit, main circuit main
module main (
  input  a,
  input  b,
  output d,
  output bo
);

  wire and_1_out, and_2_out, not_1_out, not_2_out, undriven, xor_1_out;

  xor xor_1 (xor_1_out, a, b);
  not not_1 (not_1_out, a);
  not not_2 (not_2_out, xor_1_out);
  and and_1 (and_1_out, not_1_out, b);
  xor xor_2 (d, xor_1_out, undriven);
  and and_2 (and_2_out, not_2_out, undriven);
  or or_1 (bo, and_2_out, and_1_out);
endmodule
